# Fritzing sketch Neptune Sketch (saved by Fritzing 0.9.2b)
breadboards: 1

parts:
  Onderdeel1 = Arduino Nano (Rev3.0)
  J1 = T Cobbler Plus
  DS2 = DS18B20 1-Wire Temperature Sensor [part_number=DS18B20]
  DS3 = DS18B20 1-Wire Temperature Sensor [part_number=DS18B20]
  R1 = Resistor [tolerance=±5% resistance=220 package=THT]
  R2 = Resistor [tolerance=±5% resistance=220 package=THT]
  pH_Circuit1 = pH Circuit
  U1 = 4RelayModule

nets:
  GND: Onderdeel1.GND, J1.GND#5, DS2.GND, DS3.GND, pH_Circuit1.GND, U1.GND
  VDD: Onderdeel1.D3, DS2.VDD, DS3.VDD, R1.Pin_0, R2.Pin_0
  N1: Onderdeel1.5V, DS2.DQ, DS3.DQ, R1.Pin_1, R2.Pin_1, pH_Circuit1.PRB
  N2: Onderdeel1.A5, J1.SCL
  N3: Onderdeel1.A4, J1.SDA
  N4: Onderdeel1.D13/SCK, pH_Circuit1.Vcc
  N5: J1.5.0V#1, U1.VCC
  N6: J1.#23, U1.IN1
  N7: J1.#24, U1.IN2
  N8: J1.#25, U1.IN3
  N9: J1.#26, U1.IN4

custom parts:
  T Cobbler Plus: The T-Cobbler Plus is an add on prototyping board from Adafruit specifically designed for the Raspberry Pi B+ that can break out all those tasty power, GPIO, I2C and SPI pins from the 40-pin header onto a solderless breadboard. This set will make "cobbling together" prototypes with the Pi super easy. The T-Cobbler Plus can plug into any solderless breadboard.
  4RelayModule: 4 relay arduino module SONGLE SRD05VDC-SL-C
