# Fritzing sketch Submerged Sensor Module (saved by Fritzing 0.9.3b)
perfboards: 1

parts:
  Onderdeel1 = Arduino Nano (Rev3.0)
  pH_Circuit1 = pH Circuit
  Pre-Assembled_Female_BNC1 = Pre-Assembled Female BNC
  Onderdeel2 = Bluetooth HC-05 Macho
  DS1 = DS18B20 1-Wire Temperature Sensor [part_number=DS18B20]
  DS2 = DS18B20 1-Wire Temperature Sensor [part_number=DS18B20]
  R1 = Resistor [tolerance=±5% resistance=4.7k package="0402 [SMD]"]  # not connected
  R2 = Resistor [tolerance=±5% resistance=4.7k package="0402 [SMD]"]  # not connected
  R3 = Resistor [tolerance=±5% resistance=4.7k package="0402 [SMD]"]  # not connected

nets:
  N1: Onderdeel1.D1/TX, Onderdeel2.RXD
  N2: Onderdeel1.D0/RX, Onderdeel2.TXD
  GND: Onderdeel1.GND, pH_Circuit1.GND#0, Onderdeel2.GND, DS1.GND, DS2.GND
  N3: Onderdeel1.D3, DS1.DQ, DS2.DQ
  VCC: Onderdeel1.5V, pH_Circuit1.Vcc, Onderdeel2.VCC, DS2.VDD
  N4: Onderdeel1.A5, pH_Circuit1.RX
  N5: Onderdeel1.A4, pH_Circuit1.TX
  N6: pH_Circuit1.PRB, Pre-Assembled_Female_BNC1.PRB
  N7: pH_Circuit1.GND#5, Pre-Assembled_Female_BNC1.GND
